# Fritzing sketch LED-CUBE (saved by Fritzing 0.8.7b)
stripboards: 1

parts:
  U1 = atmega328 [package=dip]
  XTAL1 = Crystal [frequency="16 Mhz" package=THT]
  C2 = Ceramic Capacitor [capacitance=100nF package="100 mil [THT, multilayer]"]
  C3 = Ceramic Capacitor [capacitance=100nF package="100 mil [THT, multilayer]"]
  S1 = Pushbutton [package="[THT]"]
  R1 = Resistor [tolerance=±5% resistance=10k package=THT]
  R2 = Resistor [tolerance=±5% resistance=150 package=THT]
  R3 = Resistor [tolerance=±5% resistance=150 package=THT]
  R4 = Resistor [tolerance=±5% resistance=150 package=THT]
  R5 = Resistor [tolerance=±5% resistance=150 package=THT]
  R6 = Resistor [tolerance=±5% resistance=150 package=THT]
  R7 = Resistor [tolerance=±5% resistance=150 package=THT]
  R8 = Resistor [tolerance=±5% resistance=150 package=THT]
  R9 = Resistor [tolerance=±5% resistance=150 package=THT]
  R10 = Resistor [tolerance=±5% resistance=150 package=THT]
  Q1 = NPN-Transistor [package="TO92 [THT]"]
  Q2 = NPN-Transistor [package="TO92 [THT]"]
  Q3 = NPN-Transistor [package="TO92 [THT]"]
  J1 = female pin header, 6 pins [form="♀ (female)"]
  CONN1 = USB connector [package=THT]
  R11 = Resistor [tolerance=±5% resistance=220 package=THT]
  R12 = Resistor [tolerance=±5% resistance=220 package=THT]
  R13 = Resistor [tolerance=±5% resistance=220 package=THT]

nets:
  N1: U1.RESET, S1.Pin_1, S1.Pin_2, R1.Pin_0
  N2: U1.D0_(RX), J1.pin3
  N3: U1.D1_(TX), J1.pin2
  N4: U1.D2, R10.Pin_1
  N5: U1.D3_(PWM), R9.Pin_1
  N6: U1.D4, R8.Pin_1
  VCC: U1.VCC, U1.AVCC, R1.Pin_1, J1.pin4, CONN1.5V
  N7: U1.GND, C2.0, C3.0, Q1.C, Q2.C, Q3.C
  N8: U1.XLAT1, XTAL1.pin_0, C3.1
  N9: U1.XLAT2, XTAL1.pin_1, C2.1
  N10: U1.D5_(PWM), R4.Pin_1
  N11: U1.D6_(PWM), R3.Pin_1
  N12: U1.D7, R7.Pin_1
  N13: U1.D8, R2.Pin_1
  N14: U1.D9_(PWM), R5.Pin_1
  N15: U1.D10_(PWM), R6.Pin_1
  N16: U1.D11_(PWM), R11.Pin_0
  N17: U1.D12, R12.Pin_0
  N18: U1.D13, R13.Pin_0
  N19: U1.AREF, S1.Pin_3, S1.Pin_4, J1.pin6, CONN1.chassis6
  N20: Q1.B, R13.Pin_1
  N21: Q2.B, R12.Pin_1
  N22: Q3.B, R11.Pin_1

notes:
  LEDs 1-9
  Ebenen 1-3
  Programmierschnittstelle
  USB Spannungsversorgung
  Reset Button
  DTR|RX|TX|+5V|CTS|GND
  -->
  NPN Transistoren
